// Logisim project ALU_2.circ as structural Verilog: 4 circuits, main circuit main
module main (
  input  [15:0] B,
  input  [15:0] A,
  input  [1:0] T,
  output [15:0] S,
  output N,
  output Z,
  output V,
  output C
);

  wire and_1_out, and_2_out, not_1_out, not_2_out, not_3_out, xor_2_out;
  wire [15:0] x0_A_B, x1_A_B, xor_1_out;
  wire [15:15] and_3_out;

  // Probe on B
  assign xor_1_out = B ^ {16{and_3_out[15]}};  // XOR_Gate xor_1, 16 bits wide
  // Probe on A
  Adder #(.width(16)) adder_1 (.a(xor_1_out), .b(A), .out(x0_A_B), .cin(and_3_out[15]), .cout(C));
  // Probe on x0_A_B
  xor xor_2 (xor_2_out, B[15], T[1]);
  assign x1_A_B = A ^ B;  // XOR_Gate xor_3, 16 bits wide
  not not_1 (not_1_out, A[15]);
  and and_1 (and_1_out, not_1_out, not_2_out, N);
  not not_2 (not_2_out, xor_2_out);
  and and_2 (and_2_out, A[15], xor_2_out, not_3_out);
  not not_3 (not_3_out, N);
  or or_1 (V, and_1_out, and_2_out);
  and and_3 (and_3_out[15], T[0], T[1]);
  MUX_4_1x16 mux_4_1x16_1 (.x3(x0_A_B), .x2(B), .x1(x1_A_B), .x0(x0_A_B), .s1(T[1]), .s0(T[0]), .out_7({N, S[14:0]}));
  nor nor_1 (Z, S[0], S[1], S[2], S[3], S[4], S[5], S[6], S[7], S[8], S[9], S[10], S[11], S[12], S[13], S[14], N);

  assign S[15] = N;

  // Other names for the same wires on the sheet: z15 = N; s1 = T[1]; x2_B[15:0] = B; x3_A_B[15:0] = x0_A_B

  // Notes on the sheet:
  //   (flag de signo)
  //   (flag de cero)
  //   (flag de debordamiento)
  //   (flag de acarreo)
  //   (RESULTADO)
endmodule

module MUX4_1 (
  input  X3,
  input  X2,
  input  s1,
  input  s0,
  input  X1,
  input  X0,
  output z
);

  wire and_1_out, and_2_out, and_3_out, and_4_out, s0_prime, s1_prime;

  not not_1 (s1_prime, s1);
  not not_2 (s0_prime, s0);
  and and_1 (and_1_out, s1, s0, X3);
  and and_2 (and_2_out, s1, s0_prime, X2);
  and and_3 (and_3_out, s1_prime, s0, X1);
  and and_4 (and_4_out, s1_prime, s0_prime, X0);
  or or_1 (z, and_1_out, and_2_out, and_3_out, and_4_out);
endmodule

module MUX_4_1x4 (
  input  [3:0] x3,
  input  [3:0] x2,
  input  [3:0] x1,
  input  [3:0] x0,
  input  s1,
  input  s0,
  output [3:0] out_7
);

  MUX4_1 mux4_1_1 (.X3(x3[3]), .X2(x2[3]), .X1(x1[3]), .X0(x0[3]), .s1(s1), .s0(s0), .z(out_7[3]));
  MUX4_1 mux4_1_2 (.X3(x3[2]), .X2(x2[2]), .X1(x1[2]), .X0(x0[2]), .s1(s1), .s0(s0), .z(out_7[2]));
  MUX4_1 mux4_1_3 (.X3(x3[1]), .X2(x2[1]), .X1(x1[1]), .X0(x0[1]), .s1(s1), .s0(s0), .z(out_7[1]));
  MUX4_1 mux4_1_4 (.X3(x3[0]), .X2(x2[0]), .X1(x1[0]), .X0(x0[0]), .s1(s1), .s0(s0), .z(out_7[0]));

  // Other names for the same wires on the sheet: x0_0 = x0[0]; x0_1 = x0[1]; x0_2 = x0[2]; x0_3 = x0[3]; x1_0 = x1[0];
  //   x1_1 = x1[1]; x1_2 = x1[2]; x1_3 = x1[3]; x2_0 = x2[0]; x2_1 = x2[1]; x2_2 = x2[2]; x2_3 = x2[3]; x3_0 = x3[0];
  //   x3_1 = x3[1]; x3_2 = x3[2]; x3_3 = x3[3]
endmodule

module MUX_4_1x16 (
  input  [15:0] x3,
  input  [15:0] x2,
  input  [15:0] x1,
  input  [15:0] x0,
  input  s1,
  input  s0,
  output [15:0] out_7
);

  MUX_4_1x4 mux_4_1x4_1 (
    .x3(x3[15:12]), .x2(x2[15:12]), .x1(x1[15:12]), .x0(x0[15:12]), .s1(s1), .s0(s0), .out_7(out_7[15:12]));
  MUX_4_1x4 mux_4_1x4_2 (
    .x3(x3[11:8]), .x2(x2[11:8]), .x1(x1[11:8]), .x0(x0[11:8]), .s1(s1), .s0(s0), .out_7(out_7[11:8]));
  MUX_4_1x4 mux_4_1x4_3 (.x3(x3[7:4]), .x2(x2[7:4]), .x1(x1[7:4]), .x0(x0[7:4]), .s1(s1), .s0(s0), .out_7(out_7[7:4]));
  MUX_4_1x4 mux_4_1x4_4 (.x3(x3[3:0]), .x2(x2[3:0]), .x1(x1[3:0]), .x0(x0[3:0]), .s1(s1), .s0(s0), .out_7(out_7[3:0]));

  // Other names for the same wires on the sheet: z0_0_3[3:0] = out_7[3:0]; z1_4_7[3:0] = out_7[7:4];
  //   z2_8_11[3:0] = out_7[11:8]; z3_12_15[3:0] = out_7[15:12]; x0_0_3[3:0] = x0[3:0]; x0_4_7[3:0] = x0[7:4];
  //   x0_8_11[3:0] = x0[11:8]; x0_12_15[3:0] = x0[15:12]; x1_0_3[3:0] = x1[3:0]; x1_4_7[3:0] = x1[7:4];
  //   x1_8_11[3:0] = x1[11:8]; x1_12_15[3:0] = x1[15:12]; x2_0_3[3:0] = x2[3:0]; x2_4_7[3:0] = x2[7:4];
  //   x2_8_11[3:0] = x2[11:8]; x2_12_15[3:0] = x2[15:12]; x3_0_3[3:0] = x3[3:0]; x3_4_7[3:0] = x3[7:4];
  //   x3_8_11[3:0] = x3[11:8]; x3_12_15[3:0] = x3[15:12]
endmodule
