// Logisim project BR32test.circ as structural Verilog: 3 circuits, main circuit main
module main (
);

  wire br32test_1_p7, br32test_1_p9, reloj_out, reset_out;
  wire [4:0] br32test_1_p8, RA, RB;
  wire [31:0] br32test_1_p10, busA, busB;

  // Probe on br32test_1_p7
  // Probe on nothing
  Clock reloj (.out(reloj_out));
  Button reset (.out(reset_out));
  BR32 br32_1 (
    .reloj(reloj_out), .reset(reset_out), .RegWr(br32test_1_p9), .RW(br32test_1_p8), .busW(br32test_1_p10),
    .RA(RA), .RB(RB), .busA(busA), .busB(busB));
  // Probe on nothing
  // BR32test br32test_1: pin names not known; wires that end beside it: RA, busA, RB, busB, reloj_out, reset_out, br32test_1_p7, br32test_1_p8, br32test_1_p9, br32test_1_p10
endmodule

module BR4 (
  input  [1:0] RA,
  input  [1:0] RB,
  input  [31:0] busW,
  input  RegWr,
  input  [1:0] RW,
  input  reloj,
  input  reset,
  output [31:0] busA,
  output [31:0] busB
);

  wire and_1_out, and_2_out, and_3_out, and_4_out, decoder_1_out0, decoder_1_out1, decoder_1_out2,
       decoder_1_out3;
  wire [31:0] register_1_q, register_2_q, register_3_q, register_4_q;

  Decoder #(.select(2), .disabled(0), .enable("false")) decoder_1 (
    .out0(decoder_1_out0), .out1(decoder_1_out1), .out2(decoder_1_out2), .out3(decoder_1_out3), .sel(RW));
  and and_1 (and_1_out, decoder_1_out0, RegWr);
  and and_2 (and_2_out, decoder_1_out1, RegWr);
  and and_3 (and_3_out, decoder_1_out2, RegWr);
  and and_4 (and_4_out, decoder_1_out3, RegWr);
  Register #(.width(32)) register_1 (.D(busW), .en(and_1_out), .Q(register_1_q), .clk(reloj), .clr(reset));
  Register #(.width(32)) register_2 (.D(busW), .en(and_2_out), .Q(register_2_q), .clk(reloj), .clr(reset));
  Register #(.width(32)) register_3 (.D(busW), .en(and_3_out), .Q(register_3_q), .clk(reloj), .clr(reset));
  Register #(.width(32)) register_4 (.D(busW), .en(and_4_out), .Q(register_4_q), .clk(reloj), .clr(reset));
  Multiplexer #(.select(2), .width(32), .enable("false")) multiplexer_1 (
    .in0(register_1_q), .in1(register_2_q), .in2(register_3_q), .in3(register_4_q), .out(busA), .sel(RA));
  Multiplexer #(.select(2), .width(32), .enable("false")) multiplexer_2 (
    .in0(register_1_q), .in1(register_2_q), .in2(register_3_q), .in3(register_4_q), .out(busB), .sel(RB));
endmodule

module BR32 (
  input  reloj,
  input  reset,
  input  RegWr,
  input  [4:0] RW,
  input  [31:0] busW,
  input  [4:0] RA,
  input  [4:0] RB,
  output [31:0] busA,
  output [31:0] busB
);

  wire and_1_out, and_2_out, and_3_out, and_4_out, and_5_out, and_6_out, and_7_out, and_8_out, en0, en1, en2,
       en3, en4, en5, en6, en7;
  wire [31:0] busA_r0_r3, busA_r4_r7, busA_r8_r11, busA_r12_r15, busA_r16_r19, busA_r20_r23, busA_r24_r27,
       busA_r28_r31, busB_r0_r3, busB_r4_r7, busB_r8_r11, busB_r12_r15, busB_r16_r19, busB_r20_r23,
       busB_r24_r27, busB_r28_r31;

  and and_1 (and_1_out, RegWr, en0);
  and and_2 (and_2_out, RegWr, en1);
  and and_3 (and_3_out, RegWr, en2);
  and and_4 (and_4_out, RegWr, en3);
  BR4 br4_1 (
    .RA(RA[1:0]), .RB(RB[1:0]), .busW(busW), .RegWr(and_1_out), .reloj(reloj), .RW(RW[1:0]),
    .busA(busA_r0_r3), .busB(busB_r0_r3), .reset(reset));
  BR4 br4_2 (
    .RA(RA[1:0]), .RB(RB[1:0]), .busW(busW), .RegWr(and_2_out), .reloj(reloj), .RW(RW[1:0]),
    .busA(busA_r4_r7), .busB(busB_r4_r7), .reset(reset));
  BR4 br4_3 (
    .RA(RA[1:0]), .RB(RB[1:0]), .busW(busW), .RegWr(and_3_out), .reloj(reloj), .RW(RW[1:0]),
    .busA(busA_r8_r11), .busB(busB_r8_r11), .reset(reset));
  BR4 br4_4 (
    .RA(RA[1:0]), .RB(RB[1:0]), .busW(busW), .RegWr(and_4_out), .reloj(reloj), .RW(RW[1:0]),
    .busA(busA_r12_r15), .busB(busB_r12_r15), .reset(reset));
  BR4 br4_5 (
    .RA(RA[1:0]), .RB(RB[1:0]), .busW(busW), .RegWr(and_5_out), .reloj(reloj), .RW(RW[1:0]),
    .busA(busA_r16_r19), .busB(busB_r16_r19), .reset(reset));
  and and_5 (and_5_out, RegWr, en4);
  BR4 br4_6 (
    .RA(RA[1:0]), .RB(RB[1:0]), .busW(busW), .RegWr(and_6_out), .reloj(reloj), .RW(RW[1:0]),
    .busA(busA_r20_r23), .busB(busB_r20_r23), .reset(reset));
  and and_6 (and_6_out, RegWr, en5);
  BR4 br4_7 (
    .RA(RA[1:0]), .RB(RB[1:0]), .busW(busW), .RegWr(and_7_out), .reloj(reloj), .RW(RW[1:0]),
    .busA(busA_r24_r27), .busB(busB_r24_r27), .reset(reset));
  and and_7 (and_7_out, RegWr, en6);
  BR4 br4_8 (
    .RA(RA[1:0]), .RB(RB[1:0]), .busW(busW), .RegWr(and_8_out), .reloj(reloj), .RW(RW[1:0]),
    .busA(busA_r28_r31), .busB(busB_r28_r31), .reset(reset));
  and and_8 (and_8_out, RegWr, en7);
  Decoder #(.select(3), .disabled(0), .enable("false")) decoder_1 (
    .out0(en0), .out1(en1), .out2(en2), .out3(en3), .out4(en4), .out5(en5), .out6(en6), .out7(en7),
    .sel(RW[4:2]));
  Multiplexer #(.select(3), .width(32), .enable("false")) multiplexer_1 (
    .in0(busA_r0_r3), .in1(busA_r4_r7), .in2(busA_r8_r11), .in3(busA_r12_r15), .in4(busA_r16_r19),
    .in5(busA_r20_r23), .in6(busA_r24_r27), .in7(busA_r28_r31), .out(busA), .sel(RA[4:2]));
  Multiplexer #(.select(3), .width(32), .enable("false")) multiplexer_2 (
    .in0(busB_r0_r3), .in1(busB_r4_r7), .in2(busB_r8_r11), .in3(busB_r12_r15), .in4(busB_r16_r19),
    .in5(busB_r20_r23), .in6(busB_r24_r27), .in7(busB_r28_r31), .out(busB), .sel(RB[4:2]));

  // Other names for the same wires on the sheet: clk = reloj; RA____xx[1:0] = RA[1:0];
  //   RA_xxx_minus_minus[2:0] = RA[4:2]; RB____xx[1:0] = RB[1:0]; RB_xxx_minus_minus[2:0] = RB[4:2];
  //   RW____xx[1:0] = RW[1:0]; RW_xxx_minus_minus[2:0] = RW[4:2]; rwr = RegWr
endmodule
