// Logisim project ROM_adder_circuit.circ as structural Verilog: 1 circuit, main circuit main
module main (
  input  in_1,
  output [7:0] out_2,
  output Error
);

  wire and_1_out, and_2_out, C8, comparator_1_eq, not_1_out, not_2_out, not_3_out, or_1_out, or_2_out, Reloj;
  wire [2:0] counter_1_q;
  wire [3:0] d_ff_1_q;
  wire [7:0] adder_1_out, rom_1_data;

  not not_1 (not_1_out, comparator_1_eq);
  not not_2 (not_2_out, C8);
  and and_1 (and_1_out, d_ff_1_q[2], comparator_1_eq, not_3_out);
  not not_3 (not_3_out, C8);
  and and_2 (and_2_out, not_1_out, d_ff_1_q[2], not_2_out);
  or or_1 (or_1_out, d_ff_1_q[3], and_1_out);
  or or_2 (or_2_out, Error, C8);
  // Probe on {Error, d_ff_1_q}
  D_Flip_Flop d_ff_1 (.clk(Reloj), .D(and_2_out), .Q(d_ff_1_q[0]), .preset(in_1));  // open: Qn, en, reset
  D_Flip_Flop d_ff_2 (.clk(Reloj), .D(d_ff_1_q[0]), .Q(d_ff_1_q[1]), .reset(in_1));  // open: Qn, preset, en
  D_Flip_Flop d_ff_3 (.clk(Reloj), .D(d_ff_1_q[1]), .Q(d_ff_1_q[2]), .reset(in_1));  // open: Qn, preset, en
  D_Flip_Flop d_ff_4 (.clk(Reloj), .D(or_1_out), .Q(d_ff_1_q[3]), .reset(in_1));  // open: Qn, preset, en
  D_Flip_Flop d_ff_5 (.clk(Reloj), .D(or_2_out), .Q(Error), .reset(in_1));  // open: Qn, preset, en
  Counter #(.width(3), .max('h7)) counter_1 (
    .load(1'b0), .count(d_ff_1_q[1]), .Q(counter_1_q), .clk(Reloj), .clr(in_1));  // open: D, carry
  ROM #(.addrWidth(3)) rom_1 (.addr(counter_1_q), .data(rom_1_data), .sel(1'b1));
  // Probe on rom_1_data
  Comparator comparator_1 (.a(rom_1_data), .b({8{1'b0}}), .eq(comparator_1_eq));  // open: gt, lt
  Adder adder_1 (.a(out_2), .b(rom_1_data), .out(adder_1_out), .cin(1'b0), .cout(C8));
  Register register_1 (.D(adder_1_out), .en(d_ff_1_q[0]), .Q(out_2), .clk(Reloj), .clr(in_1));
  Clock #(.highDuration(100), .lowDuration(100)) clock_1 (.out(Reloj));
  // Probe on out_2

  // Other names for the same wires on the sheet: OV = Error; reset = in_1

  // Notes on the sheet:
  //   contents of rom_1 (hex, n*v repeats v):
  //   35 2a 5 46 2 13 94
endmodule
