// Logisim project Sequential_Multiplier.circ as structural Verilog: 1 circuit, main circuit main
module main (
  input  [7:0] cte1,
  input  [7:0] cte2,
  input  in_3,
  output [15:0] P
);

  wire and_1_out, and_2_out, comparator_1_eq, not_1_out, or_1_out, Reloj;
  wire [2:0] d_ff_1_q;
  wire [7:0] counter_1_q;
  wire [15:0] adder_1_out;

  Clock #(.highDuration(100), .lowDuration(100)) clock_1 (.out(Reloj));
  // Probe on d_ff_1_q
  not not_1 (not_1_out, comparator_1_eq);
  or or_1 (or_1_out, d_ff_1_q[2], and_1_out);
  and and_1 (and_1_out, d_ff_1_q[1], comparator_1_eq);
  and and_2 (and_2_out, not_1_out, d_ff_1_q[1]);
  D_Flip_Flop d_ff_1 (.clk(Reloj), .D(and_2_out), .Q(d_ff_1_q[0]), .preset(in_3));  // open: Qn, en, reset
  D_Flip_Flop d_ff_2 (.clk(Reloj), .D(d_ff_1_q[0]), .Q(d_ff_1_q[1]), .reset(in_3));  // open: Qn, preset, en
  D_Flip_Flop d_ff_3 (.clk(Reloj), .D(or_1_out), .Q(d_ff_1_q[2]), .reset(in_3));  // open: Qn, preset, en
  Counter counter_1 (.load(1'b0), .count(d_ff_1_q[0]), .Q(counter_1_q), .clk(Reloj), .clr(in_3));  // open: D, carry
  Adder #(.width(16)) adder_1 (.a(P), .b({{8{1'b0}}, cte1}), .out(adder_1_out), .cin(1'b0));  // open: cout
  Register #(.width(16)) register_1 (.D(adder_1_out), .en(d_ff_1_q[1]), .Q(P), .clk(Reloj), .clr(in_3));
  // Probe on counter_1_q
  Comparator comparator_1 (.a(counter_1_q), .b(cte2), .eq(comparator_1_eq));  // open: gt, lt

  // Other names for the same wires on the sheet: reset = in_3
endmodule
