// Logisim project cache.circ as structural Verilog: 1 circuit, main circuit main
module main (
  input  in_1
);

  wire clk, comparator_1_eq, comparator_2_eq, decoder_1_out1, decoder_1_out2, decoder_1_out3, decoder_1_out4,
       decoder_1_out5, decoder_1_out6, decoder_1_out7, decoder_1_out8, decoder_1_out9, decoder_1_out10,
       decoder_1_out11, hit, mem_en, not_1_out, not_2_out, not_3_out, not_5_out, not_6_out, or_1_out,
       or_2_out, r0, r1, r2, r3, ram_1_data, str0, str1, str_via, via, write_c;
  wire [3:0] counter_1_q;
  wire [7:0] ram_2_data, ram_3_data;
  wire [15:0] counter_2_q, dir;
  wire [31:0] bus, inst, multiplexer_2_out, multiplexer_4_out, ram_4_data, ram_5_data, ram_6_data,
       ram_7_data, ram_8_data, ram_9_data, ram_10_data, ram_11_data, w0, w1, w2, w3;

  not not_1 (not_1_out, ram_1_data);
  Clock clock_1 (.out(clk));
  RAM #(.addrWidth(5), .dataWidth(1), .bus("separate")) ram_1 (
    .addr(dir[8:4]), .din(not_1_out), .data(ram_1_data), .str(str_via), .clk(clk), .clr(in_1));  // open: sel, ld
  and and_1 (str0, write_c, not_2_out);
  not not_2 (not_2_out, via);
  Comparator comparator_1 (.a(ram_2_data), .b({1'b1, dir[15:9]}), .eq(comparator_1_eq));  // open: gt, lt
  Multiplexer #(.disabled(0), .enable("false")) multiplexer_1 (
    .in0(ram_1_data), .in1(comparator_2_eq), .out(via), .sel(hit));
  // Probe on nothing
  or or_1 (or_1_out, comparator_1_eq, comparator_2_eq);
  not not_3 (not_3_out, write_c);
  and and_2 (hit, or_1_out, not_3_out);
  not not_4 (mem_en, hit);
  // Probe on nothing
  // Probe on nothing
  // cache_test5 cache_test5_1: pin names not known; wires that end beside it: dir, inst, hit, via, dir[8:4], clk, in_1, 20'hdb059
  // Probe on 20'hdb059
  RAM #(.addrWidth(5), .bus("separate")) ram_2 (
    .addr(dir[8:4]), .din({1'b1, dir[15:9]}), .data(ram_2_data), .str(str0), .clk(clk), .clr(in_1));  // open: sel, ld
  and and_3 (str1, write_c, via);
  Comparator comparator_2 (.a(ram_3_data), .b({1'b1, dir[15:9]}), .eq(comparator_2_eq));  // open: gt, lt
  RAM #(.addrWidth(5), .bus("separate")) ram_3 (
    .addr(dir[8:4]), .din({1'b1, dir[15:9]}), .data(ram_3_data), .str(str1), .clk(clk), .clr(in_1));  // open: sel, ld
  Register #(.width(32)) register_1 (.D(bus), .en(r0), .Q(w0), .clk(clk), .clr(in_1));
  Counter #(.width(4), .max('hf)) counter_1 (
    .Q(counter_1_q), .clk(clk), .clr(or_2_out));  // open: load, D, count, carry
  or or_2 (or_2_out, not_5_out, in_1);
  not not_5 (not_5_out, mem_en);
  Decoder #(.select(4), .disabled(0), .enable("false")) decoder_1 (
    .out1(decoder_1_out1), .out2(decoder_1_out2), .out3(decoder_1_out3), .out4(decoder_1_out4),
    .out5(decoder_1_out5), .out6(decoder_1_out6), .out7(decoder_1_out7), .out8(decoder_1_out8),
    .out9(decoder_1_out9), .out10(decoder_1_out10), .out11(decoder_1_out11), .sel(counter_1_q));  // open: out0, out12, out13, out14, out15
  or or_3 (r0, decoder_1_out4, decoder_1_out5);
  or or_4 (r1, decoder_1_out6, decoder_1_out7);
  Register #(.width(32)) register_2 (.D(bus), .en(r1), .Q(w1), .clk(clk), .clr(in_1));
  RAM #(.addrWidth(5), .dataWidth(32), .bus("separate")) ram_4 (
    .addr(dir[8:4]), .din(w0), .data(ram_4_data), .str(str0), .clk(clk), .clr(in_1));  // open: sel, ld
  or or_5 (r3, decoder_1_out10, decoder_1_out11);
  or or_6 (r2, decoder_1_out8, decoder_1_out9);
  Register #(.width(32)) register_3 (.D(bus), .en(r2), .Q(w2), .clk(clk), .clr(in_1));
  or or_7 (write_c, decoder_1_out1, decoder_1_out2, decoder_1_out3, decoder_1_out4, decoder_1_out5, decoder_1_out6, decoder_1_out7, decoder_1_out8, decoder_1_out9, decoder_1_out10, decoder_1_out11);
  D_Flip_Flop d_ff_1 (.clk(clk), .D(decoder_1_out11), .Q(str_via), .reset(in_1));  // open: Qn, preset, en
  Register #(.width(32)) register_4 (.D(bus), .en(r3), .Q(w3), .clk(clk), .clr(in_1));
  RAM #(.addrWidth(5), .dataWidth(32), .bus("separate")) ram_5 (
    .addr(dir[8:4]), .din(w1), .data(ram_5_data), .str(str0), .clk(clk), .clr(in_1));  // open: sel, ld
  RAM #(.addrWidth(5), .dataWidth(32), .bus("separate")) ram_6 (
    .addr(dir[8:4]), .din(w2), .data(ram_6_data), .str(str0), .clk(clk), .clr(in_1));  // open: sel, ld
  Multiplexer #(.select(2), .width(32), .enable("false")) multiplexer_2 (
    .in0(ram_4_data), .in1(ram_5_data), .in2(ram_6_data), .in3(ram_7_data), .out(multiplexer_2_out),
    .sel(dir[3:2]));
  RAM #(.addrWidth(5), .dataWidth(32), .bus("separate")) ram_7 (
    .addr(dir[8:4]), .din(w3), .data(ram_7_data), .str(str0), .clk(clk), .clr(in_1));  // open: sel, ld
  Multiplexer #(.width(32), .enable("false")) multiplexer_3 (
    .in0(multiplexer_2_out), .in1(multiplexer_4_out), .out(inst), .sel(via));
  Multiplexer #(.select(2), .width(32), .enable("false")) multiplexer_4 (
    .in0(ram_8_data), .in1(ram_9_data), .in2(ram_10_data), .in3(ram_11_data), .out(multiplexer_4_out),
    .sel(dir[3:2]));
  RAM #(.addrWidth(5), .dataWidth(32), .bus("separate")) ram_8 (
    .addr(dir[8:4]), .din(w0), .data(ram_8_data), .str(str1), .clk(clk), .clr(in_1));  // open: sel, ld
  // MP_main main_1: pin names not known; wires that end beside it: dir, mem_en, clk, in_1, bus
  RAM #(.addrWidth(5), .dataWidth(32), .bus("separate")) ram_9 (
    .addr(dir[8:4]), .din(w1), .data(ram_9_data), .str(str1), .clk(clk), .clr(in_1));  // open: sel, ld
  RAM #(.addrWidth(5), .dataWidth(32), .bus("separate")) ram_10 (
    .addr(dir[8:4]), .din(w2), .data(ram_10_data), .str(str1), .clk(clk), .clr(in_1));  // open: sel, ld
  ROM #(.addrWidth(16), .dataWidth(16)) rom_1 (.addr(counter_2_q), .data(dir), .sel(1'b1));
  RAM #(.addrWidth(5), .dataWidth(32), .bus("separate")) ram_11 (
    .addr(dir[8:4]), .din(w3), .data(ram_11_data), .str(str1), .clk(clk), .clr(in_1));  // open: sel, ld
  Counter #(.width(16), .max('hffff)) counter_2 (
    .count(not_6_out), .Q(counter_2_q), .clk(clk), .clr(in_1));  // open: load, D, carry
  not not_6 (not_6_out, mem_en);

  // Other names for the same wires on the sheet: clr = in_1; word[3:0] = dir[3:0]; set[4:0] = dir[8:4];
  //   tag[6:0] = dir[15:9]

  // Notes on the sheet:
  //   RAM 32x1b
  //   RAM 32x8b
  //   RAM 32x8b
  //   Unidad de Control
  //   RAM 32x32b
  //   RAM 32x32b
  //   RAM 32x32b
  //   RAM 32x32b
  //   RAM 32x32b
  //   RAM 32x32b
  //   RAM 32x32b
  //   contents of rom_1 (hex, n*v repeats v):
  //   200 400 600 404 2b0 4b0 6b0 6b4 800 a00 c00 a04
  //   RAM 32x32b
endmodule
